# Fritzing sketch capacitive_touch (saved by Fritzing 1.0.3b)
breadboards: 1

parts:
  Part1 = Arduino Uno (Rev3)
  R1 = Resistor [tolerance=±5% resistance=1M power=0.25W package=THT]

nets:
  N1: Part1.D2, R1.Pin_1
  N2: Part1.5V, R1.Pin_0

notes:
  Use some cunductive material at the end of this wire. Cupper foil, a paper clip something else
